// Logisim project CIS272EC1.circ as structural Verilog: 5 circuits, main circuit Main
module Main (
  input  Write_0,
  input  Write_1,
  input  Write_2,
  input  Write_3,
  input  Write_4,
  input  Write_5,
  input  Write_6,
  input  Write_7,
  input  Write_8,
  input  Write_9,
  input  Write_10,
  input  Write_11,
  input  Write_12,
  input  Write_13,
  input  Write_14,
  input  Write_15,
  input  R0,
  input  R1,
  input  R2,
  input  Write_Enable,
  output Bit_0,
  output Bit_1,
  output Bit_2,
  output Bit_3,
  output Bit_4,
  output Bit_5,
  output Bit_6,
  output Bit_7,
  output Bit_8,
  output Bit_9,
  output Bit_10,
  output Bit_11,
  output Bit_12,
  output Bit_13,
  output Bit_14,
  output Bit_15
);

  Multiple_Registers multiple_registers_1 (
    .Write_0(Write_0), .Write_1(Write_1), .Write_2(Write_2), .Write_3(Write_3), .Write_4(Write_4),
    .Write_5(Write_5), .Write_6(Write_6), .Write_7(Write_7), .Write_8(Write_8), .Write_9(Write_9),
    .Write_10(Write_10), .Write_11(Write_11), .Write_12(Write_12), .Write_13(Write_13), .Write_14(Write_14),
    .Write_15(Write_15), .Clk(Write_Enable), .R0(R2), .R1(R1), .R2(R0), .Bit_0(Bit_0), .Bit_1(Bit_1),
    .Bit_2(Bit_2), .Bit_3(Bit_3), .Bit_4(Bit_4), .Bit_5(Bit_5), .Bit_6(Bit_6), .Bit_7(Bit_7), .Bit_8(Bit_8),
    .Bit_9(Bit_9), .Bit_10(Bit_10), .Bit_11(Bit_11), .Bit_12(Bit_12), .Bit_13(Bit_13), .Bit_14(Bit_14),
    .Bit_15(Bit_15));
endmodule

module Register (
  input  Clock,
  input  Start,
  input  Write_0,
  input  Write_1,
  input  Write_2,
  input  Write_3,
  input  Write_4,
  input  Write_5,
  input  Write_6,
  input  Write_7,
  input  Write_8,
  input  Write_9,
  input  Write_10,
  input  Write_11,
  input  Write_12,
  input  Write_13,
  input  Write_14,
  input  Write_15,
  output Bit_0,
  output Bit_1,
  output Bit_2,
  output Bit_3,
  output Bit_4,
  output Bit_5,
  output Bit_6,
  output Bit_7,
  output Bit_8,
  output Bit_9,
  output Bit_10,
  output Bit_11,
  output Bit_12,
  output Bit_13,
  output Bit_14,
  output Bit_15
);

  D_Flip_Flop d_ff_1 (.clk(Clock), .D(Write_0), .Q(Bit_0), .en(Start));  // open: Qn, preset, reset
  D_Flip_Flop d_ff_2 (.clk(Clock), .D(Write_1), .Q(Bit_1), .en(Start));  // open: Qn, preset, reset
  D_Flip_Flop d_ff_3 (.clk(Clock), .D(Write_2), .Q(Bit_2), .en(Start));  // open: Qn, preset, reset
  D_Flip_Flop d_ff_4 (.clk(Clock), .D(Write_3), .Q(Bit_3), .en(Start));  // open: Qn, preset, reset
  D_Flip_Flop d_ff_5 (.clk(Clock), .D(Write_4), .Q(Bit_4), .en(Start));  // open: Qn, preset, reset
  D_Flip_Flop d_ff_6 (.clk(Clock), .D(Write_5), .Q(Bit_5), .en(Start));  // open: Qn, preset, reset
  D_Flip_Flop d_ff_7 (.clk(Clock), .D(Write_6), .Q(Bit_6), .en(Start));  // open: Qn, preset, reset
  D_Flip_Flop d_ff_8 (.clk(Clock), .D(Write_7), .Q(Bit_7), .en(Start));  // open: Qn, preset, reset
  D_Flip_Flop d_ff_9 (.clk(Clock), .D(Write_8), .Q(Bit_8), .en(Start));  // open: Qn, preset, reset
  D_Flip_Flop d_ff_10 (.clk(Clock), .D(Write_9), .Q(Bit_9), .en(Start));  // open: Qn, preset, reset
  D_Flip_Flop d_ff_11 (.clk(Clock), .D(Write_10), .Q(Bit_10), .en(Start));  // open: Qn, preset, reset
  D_Flip_Flop d_ff_12 (.clk(Clock), .D(Write_11), .Q(Bit_11), .en(Start));  // open: Qn, preset, reset
  D_Flip_Flop d_ff_13 (.clk(Clock), .D(Write_12), .Q(Bit_12), .en(Start));  // open: Qn, preset, reset
  D_Flip_Flop d_ff_14 (.clk(Clock), .D(Write_13), .Q(Bit_13), .en(Start));  // open: Qn, preset, reset
  D_Flip_Flop d_ff_15 (.clk(Clock), .D(Write_14), .Q(Bit_14), .en(Start));  // open: Qn, preset, reset
  D_Flip_Flop d_ff_16 (.clk(Clock), .D(Write_15), .Q(Bit_15), .en(Start));  // open: Qn, preset, reset
endmodule

// Register
module Multiple_Registers (
  input  Write_0,
  input  Write_1,
  input  Write_2,
  input  Write_3,
  input  Write_4,
  input  Write_5,
  input  Write_6,
  input  Write_7,
  input  Write_8,
  input  Write_9,
  input  Write_10,
  input  Write_11,
  input  Write_12,
  input  Write_13,
  input  Write_14,
  input  Write_15,
  input  Clk,
  input  R0,
  input  R1,
  input  R2,
  output Bit_0,
  output Bit_1,
  output Bit_2,
  output Bit_3,
  output Bit_4,
  output Bit_5,
  output Bit_6,
  output Bit_7,
  output Bit_8,
  output Bit_9,
  output Bit_10,
  output Bit_11,
  output Bit_12,
  output Bit_13,
  output Bit_14,
  output Bit_15
);

  wire _16_Bit_OR_bit_0, _16_Bit_OR_bit_0_2, _16_Bit_OR_bit_1, _16_Bit_OR_bit_1_2, _16_Bit_OR_bit_2,
       _16_Bit_OR_bit_2_2, _16_Bit_OR_bit_3, _16_Bit_OR_bit_3_2, _16_Bit_OR_bit_4, _16_Bit_OR_bit_4_2,
       _16_Bit_OR_bit_5, _16_Bit_OR_bit_5_2, _16_Bit_OR_bit_6, _16_Bit_OR_bit_6_2, _16_Bit_OR_bit_7,
       _16_Bit_OR_bit_7_2, bit_read_1_bit_0, bit_read_1_bit_1, bit_read_1_bit_2, bit_read_1_bit_3,
       bit_read_1_bit_4, bit_read_1_bit_5, bit_read_1_bit_6, bit_read_1_bit_7, bit_read_1_bit_8,
       bit_read_1_bit_9, bit_read_1_bit_10, bit_read_1_bit_11, bit_read_1_bit_12, bit_read_1_bit_13,
       bit_read_1_bit_14, bit_read_1_bit_15, bit_read_2_bit_0, bit_read_2_bit_1, bit_read_2_bit_2,
       bit_read_2_bit_3, bit_read_2_bit_4, bit_read_2_bit_5, bit_read_2_bit_6, bit_read_2_bit_7,
       bit_read_2_bit_8, bit_read_2_bit_9, bit_read_2_bit_10, bit_read_2_bit_11, bit_read_2_bit_12,
       bit_read_2_bit_13, bit_read_2_bit_14, bit_read_2_bit_15, bit_read_3_bit_0, bit_read_3_bit_1,
       bit_read_3_bit_2, bit_read_3_bit_3, bit_read_3_bit_4, bit_read_3_bit_5, bit_read_3_bit_6,
       bit_read_3_bit_7, bit_read_3_bit_8, bit_read_3_bit_9, bit_read_3_bit_10, bit_read_3_bit_11,
       bit_read_3_bit_12, bit_read_3_bit_13, bit_read_3_bit_14, bit_read_3_bit_15, Register_0_bit_0,
       Register_0_bit_1, Register_0_bit_2, Register_0_bit_3, Register_0_bit_4, Register_0_bit_5,
       Register_0_bit_6, Register_0_bit_7, Register_0_bit_8, Register_0_bit_9, Register_0_bit_10,
       Register_0_bit_11, Register_0_bit_12, Register_0_bit_13, Register_0_bit_14, Register_0_bit_15,
       Register_1_bit_0, Register_1_bit_1, Register_1_bit_2, Register_1_bit_3, Register_1_bit_4,
       Register_1_bit_5, Register_1_bit_6, Register_1_bit_7, Register_1_bit_8, Register_1_bit_9,
       Register_1_bit_10, Register_1_bit_11, Register_1_bit_12, Register_1_bit_13, Register_1_bit_14,
       Register_1_bit_15, Register_bit_0, Register_bit_1, Register_bit_2, Register_bit_3, Register_bit_4,
       Register_bit_5, Register_bit_6, Register_bit_7, Register_bit_8, Register_bit_9, Register_bit_10,
       Register_bit_11, Register_bit_12, Register_bit_13, Register_bit_14, Register_bit_15;

  Register Register_1 (
    .Start(R1), .Write_0(Write_0), .Write_1(Write_1), .Write_2(Write_2), .Write_3(Write_3),
    .Write_4(Write_4), .Write_5(Write_5), .Write_6(Write_6), .Write_7(Write_7), .Write_8(Write_8),
    .Write_9(Write_9), .Write_10(Write_10), .Write_11(Write_11), .Write_12(Write_12), .Write_13(Write_13),
    .Write_14(Write_14), .Write_15(Write_15), .Clock(Clk), .Bit_0(Register_1_bit_0),
    .Bit_1(Register_1_bit_1), .Bit_2(Register_1_bit_2), .Bit_3(Register_1_bit_3), .Bit_4(Register_1_bit_4),
    .Bit_5(Register_1_bit_5), .Bit_6(Register_1_bit_6), .Bit_7(Register_1_bit_7), .Bit_8(Register_1_bit_8),
    .Bit_9(Register_1_bit_9), .Bit_10(Register_1_bit_10), .Bit_11(Register_1_bit_11),
    .Bit_12(Register_1_bit_12), .Bit_13(Register_1_bit_13), .Bit_14(Register_1_bit_14),
    .Bit_15(Register_1_bit_15));
  Register Register (
    .Start(R2), .Write_0(Write_0), .Write_1(Write_1), .Write_2(Write_2), .Write_3(Write_3),
    .Write_4(Write_4), .Write_5(Write_5), .Write_6(Write_6), .Write_7(Write_7), .Write_8(Write_8),
    .Write_9(Write_9), .Write_10(Write_10), .Write_11(Write_11), .Write_12(Write_12), .Write_13(Write_13),
    .Write_14(Write_14), .Write_15(Write_15), .Clock(Clk), .Bit_0(Register_bit_0), .Bit_1(Register_bit_1),
    .Bit_2(Register_bit_2), .Bit_3(Register_bit_3), .Bit_4(Register_bit_4), .Bit_5(Register_bit_5),
    .Bit_6(Register_bit_6), .Bit_7(Register_bit_7), .Bit_8(Register_bit_8), .Bit_9(Register_bit_9),
    .Bit_10(Register_bit_10), .Bit_11(Register_bit_11), .Bit_12(Register_bit_12), .Bit_13(Register_bit_13),
    .Bit_14(Register_bit_14), .Bit_15(Register_bit_15));
  Register Register_0 (
    .Start(R0), .Write_0(Write_0), .Write_1(Write_1), .Write_2(Write_2), .Write_3(Write_3),
    .Write_4(Write_4), .Write_5(Write_5), .Write_6(Write_6), .Write_7(Write_7), .Write_8(Write_8),
    .Write_9(Write_9), .Write_10(Write_10), .Write_11(Write_11), .Write_12(Write_12), .Write_13(Write_13),
    .Write_14(Write_14), .Write_15(Write_15), .Clock(Clk), .Bit_0(Register_0_bit_0),
    .Bit_1(Register_0_bit_1), .Bit_2(Register_0_bit_2), .Bit_3(Register_0_bit_3), .Bit_4(Register_0_bit_4),
    .Bit_5(Register_0_bit_5), .Bit_6(Register_0_bit_6), .Bit_7(Register_0_bit_7), .Bit_8(Register_0_bit_8),
    .Bit_9(Register_0_bit_9), .Bit_10(Register_0_bit_10), .Bit_11(Register_0_bit_11),
    .Bit_12(Register_0_bit_12), .Bit_13(Register_0_bit_13), .Bit_14(Register_0_bit_14),
    .Bit_15(Register_0_bit_15));
  Bit_Read_Gate bit_read_1 (
    .Read(R0), .B0(Register_0_bit_0), .B1(Register_0_bit_1), .B2(Register_0_bit_2), .B3(Register_0_bit_3),
    .B4(Register_0_bit_4), .B5(Register_0_bit_5), .B6(Register_0_bit_6), .B7(Register_0_bit_7),
    .B8(Register_0_bit_8), .B9(Register_0_bit_9), .B10(Register_0_bit_10), .B11(Register_0_bit_11),
    .B12(Register_0_bit_12), .B13(Register_0_bit_13), .B14(Register_0_bit_14), .B15(Register_0_bit_15),
    .Bit_0(bit_read_1_bit_0), .Bit_1(bit_read_1_bit_1), .Bit_2(bit_read_1_bit_2), .Bit_3(bit_read_1_bit_3),
    .Bit_4(bit_read_1_bit_4), .Bit_5(bit_read_1_bit_5), .Bit_6(bit_read_1_bit_6), .Bit_7(bit_read_1_bit_7),
    .Bit_8(bit_read_1_bit_8), .Bit_9(bit_read_1_bit_9), .Bit_10(bit_read_1_bit_10),
    .Bit_11(bit_read_1_bit_11), .BIt_12(bit_read_1_bit_12), .Bit_13(bit_read_1_bit_13),
    .Bit_14(bit_read_1_bit_14), .Bit_15(bit_read_1_bit_15));
  Bit_Read_Gate bit_read_2 (
    .Read(R1), .B0(Register_1_bit_0), .B1(Register_1_bit_1), .B2(Register_1_bit_2), .B3(Register_1_bit_3),
    .B4(Register_1_bit_4), .B5(Register_1_bit_5), .B6(Register_1_bit_6), .B7(Register_1_bit_7),
    .B8(Register_1_bit_8), .B9(Register_1_bit_9), .B10(Register_1_bit_10), .B11(Register_1_bit_11),
    .B12(Register_1_bit_12), .B13(Register_1_bit_13), .B14(Register_1_bit_14), .B15(Register_1_bit_15),
    .Bit_0(bit_read_2_bit_0), .Bit_1(bit_read_2_bit_1), .Bit_2(bit_read_2_bit_2), .Bit_3(bit_read_2_bit_3),
    .Bit_4(bit_read_2_bit_4), .Bit_5(bit_read_2_bit_5), .Bit_6(bit_read_2_bit_6), .Bit_7(bit_read_2_bit_7),
    .Bit_8(bit_read_2_bit_8), .Bit_9(bit_read_2_bit_9), .Bit_10(bit_read_2_bit_10),
    .Bit_11(bit_read_2_bit_11), .BIt_12(bit_read_2_bit_12), .Bit_13(bit_read_2_bit_13),
    .Bit_14(bit_read_2_bit_14), .Bit_15(bit_read_2_bit_15));
  Bit_Read_Gate bit_read_3 (
    .Read(R2), .B0(Register_bit_0), .B1(Register_bit_1), .B2(Register_bit_2), .B3(Register_bit_3),
    .B4(Register_bit_4), .B5(Register_bit_5), .B6(Register_bit_6), .B7(Register_bit_7), .B8(Register_bit_8),
    .B9(Register_bit_9), .B10(Register_bit_10), .B11(Register_bit_11), .B12(Register_bit_12),
    .B13(Register_bit_13), .B14(Register_bit_14), .B15(Register_bit_15), .Bit_0(bit_read_3_bit_0),
    .Bit_1(bit_read_3_bit_1), .Bit_2(bit_read_3_bit_2), .Bit_3(bit_read_3_bit_3), .Bit_4(bit_read_3_bit_4),
    .Bit_5(bit_read_3_bit_5), .Bit_6(bit_read_3_bit_6), .Bit_7(bit_read_3_bit_7), .Bit_8(bit_read_3_bit_8),
    .Bit_9(bit_read_3_bit_9), .Bit_10(bit_read_3_bit_10), .Bit_11(bit_read_3_bit_11),
    .BIt_12(bit_read_3_bit_12), .Bit_13(bit_read_3_bit_13), .Bit_14(bit_read_3_bit_14),
    .Bit_15(bit_read_3_bit_15));
  _16_bit_OR u_16_bit_or_1 (
    ._0A(bit_read_1_bit_0), ._0B(_16_Bit_OR_bit_0), ._1A(bit_read_1_bit_1), ._1B(_16_Bit_OR_bit_1),
    ._2A(bit_read_1_bit_2), ._2B(_16_Bit_OR_bit_2), ._3A(bit_read_1_bit_3), ._3B(_16_Bit_OR_bit_3),
    ._4A(bit_read_1_bit_4), ._4B(_16_Bit_OR_bit_4), ._5A(bit_read_1_bit_5), ._5B(_16_Bit_OR_bit_5),
    ._6A(bit_read_1_bit_6), ._6B(_16_Bit_OR_bit_6), ._7A(bit_read_1_bit_7), ._7B(_16_Bit_OR_bit_7),
    ._8A(bit_read_1_bit_8), ._8B(_16_Bit_OR_bit_0_2), ._9A(bit_read_1_bit_9), ._9B(_16_Bit_OR_bit_1_2),
    ._10A(bit_read_1_bit_10), ._10B(_16_Bit_OR_bit_2_2), ._11A(bit_read_1_bit_11), ._11B(_16_Bit_OR_bit_3_2),
    ._12A(bit_read_1_bit_12), ._12B(_16_Bit_OR_bit_4_2), ._13A(bit_read_1_bit_13), ._13B(_16_Bit_OR_bit_5_2),
    ._14A(bit_read_1_bit_14), ._14B(_16_Bit_OR_bit_6_2), ._15A(bit_read_1_bit_15), ._15B(_16_Bit_OR_bit_7_2),
    .Bit_0(Bit_0), .Bit_1(Bit_1), .Bit_2(Bit_2), .Bit_3(Bit_3), .Bit_4(Bit_4), .Bit_5(Bit_5), .Bit_6(Bit_6),
    .Bit_7(Bit_7), .Bit_0_2(Bit_8), .Bit_1_2(Bit_9), .Bit_2_2(Bit_10), .Bit_3_2(Bit_11), .Bit_4_2(Bit_12),
    .Bit_5_2(Bit_13), .Bit_6_2(Bit_14), .Bit_7_2(Bit_15));
  _16_bit_OR _16_Bit_OR (
    ._0A(bit_read_2_bit_0), ._0B(bit_read_3_bit_0), ._1A(bit_read_2_bit_1), ._1B(bit_read_3_bit_1),
    ._2A(bit_read_2_bit_2), ._2B(bit_read_3_bit_2), ._3A(bit_read_2_bit_3), ._3B(bit_read_3_bit_3),
    ._4A(bit_read_2_bit_4), ._4B(bit_read_3_bit_4), ._5A(bit_read_2_bit_5), ._5B(bit_read_3_bit_5),
    ._6A(bit_read_2_bit_6), ._6B(bit_read_3_bit_6), ._7A(bit_read_2_bit_7), ._7B(bit_read_3_bit_7),
    ._8A(bit_read_2_bit_8), ._8B(bit_read_3_bit_8), ._9A(bit_read_2_bit_9), ._9B(bit_read_3_bit_9),
    ._10A(bit_read_2_bit_10), ._10B(bit_read_3_bit_10), ._11A(bit_read_2_bit_11), ._11B(bit_read_3_bit_11),
    ._12A(bit_read_2_bit_12), ._12B(bit_read_3_bit_12), ._13A(bit_read_2_bit_13), ._13B(bit_read_3_bit_13),
    ._14A(bit_read_2_bit_14), ._14B(bit_read_3_bit_14), ._15A(bit_read_2_bit_15), ._15B(bit_read_3_bit_15),
    .Bit_0(_16_Bit_OR_bit_0), .Bit_1(_16_Bit_OR_bit_1), .Bit_2(_16_Bit_OR_bit_2), .Bit_3(_16_Bit_OR_bit_3),
    .Bit_4(_16_Bit_OR_bit_4), .Bit_5(_16_Bit_OR_bit_5), .Bit_6(_16_Bit_OR_bit_6), .Bit_7(_16_Bit_OR_bit_7),
    .Bit_0_2(_16_Bit_OR_bit_0_2), .Bit_1_2(_16_Bit_OR_bit_1_2), .Bit_2_2(_16_Bit_OR_bit_2_2),
    .Bit_3_2(_16_Bit_OR_bit_3_2), .Bit_4_2(_16_Bit_OR_bit_4_2), .Bit_5_2(_16_Bit_OR_bit_5_2),
    .Bit_6_2(_16_Bit_OR_bit_6_2), .Bit_7_2(_16_Bit_OR_bit_7_2));
endmodule

// Bit Read Gate
module Bit_Read_Gate (
  input  Read,
  input  B0,
  input  B1,
  input  B2,
  input  B3,
  input  B4,
  input  B5,
  input  B6,
  input  B7,
  input  B8,
  input  B9,
  input  B10,
  input  B11,
  input  B12,
  input  B13,
  input  B14,
  input  B15,
  output Bit_0,
  output Bit_1,
  output Bit_2,
  output Bit_3,
  output Bit_4,
  output Bit_5,
  output Bit_6,
  output Bit_7,
  output Bit_8,
  output Bit_9,
  output Bit_10,
  output Bit_11,
  output BIt_12,
  output Bit_13,
  output Bit_14,
  output Bit_15
);

  and and_1 (Bit_0, B0, Read);
  and and_2 (Bit_1, B1, Read);
  and and_3 (Bit_2, B2, Read);
  and and_4 (Bit_3, B3, Read);
  and and_5 (Bit_4, B4, Read);
  and and_6 (Bit_5, B5, Read);
  and and_7 (Bit_6, B6, Read);
  and and_8 (Bit_7, B7, Read);
  and and_9 (Bit_8, B8, Read);
  and and_10 (Bit_9, B9, Read);
  and and_11 (Bit_10, B10, Read);
  and and_12 (Bit_11, B11, Read);
  and and_13 (BIt_12, B12, Read);
  and and_14 (Bit_13, B13, Read);
  and and_15 (Bit_14, B14, Read);
  and and_16 (Bit_15, B15, Read);
endmodule

// 16 Bit OR
module _16_bit_OR (
  input  _0A,
  input  _0B,
  input  _1A,
  input  _1B,
  input  _2A,
  input  _2B,
  input  _3A,
  input  _3B,
  input  _4A,
  input  _4B,
  input  _5A,
  input  _5B,
  input  _6A,
  input  _6B,
  input  _7A,
  input  _7B,
  input  _8A,
  input  _8B,
  input  _9A,
  input  _9B,
  input  _10A,
  input  _10B,
  input  _11A,
  input  _11B,
  input  _12A,
  input  _12B,
  input  _13A,
  input  _13B,
  input  _14A,
  input  _14B,
  input  _15A,
  input  _15B,
  output Bit_0,
  output Bit_1,
  output Bit_2,
  output Bit_3,
  output Bit_4,
  output Bit_5,
  output Bit_6,
  output Bit_7,
  output Bit_0_2,
  output Bit_1_2,
  output Bit_2_2,
  output Bit_3_2,
  output Bit_4_2,
  output Bit_5_2,
  output Bit_6_2,
  output Bit_7_2
);

  or or_1 (Bit_0, _0A, _0B);
  or or_2 (Bit_1, _1A, _1B);
  or or_3 (Bit_2, _2A, _2B);
  or or_4 (Bit_3, _3A, _3B);
  or or_5 (Bit_4, _4A, _4B);
  or or_6 (Bit_5, _5A, _5B);
  or or_7 (Bit_6, _6A, _6B);
  or or_8 (Bit_7, _7A, _7B);
  or or_9 (Bit_0_2, _8A, _8B);
  or or_10 (Bit_1_2, _9A, _9B);
  or or_11 (Bit_2_2, _10A, _10B);
  or or_12 (Bit_3_2, _11A, _11B);
  or or_13 (Bit_4_2, _12A, _12B);
  or or_14 (Bit_5_2, _13A, _13B);
  or or_15 (Bit_6_2, _14A, _14B);
  or or_16 (Bit_7_2, _15A, _15B);
endmodule
