// Logisim project McDermottJ_Lab1b.circ as structural Verilog: 1 circuit, main circuit main
module main (
  input  a,
  input  b,
  output intermediate_1,
  output main,
  output intermediate_2
);

  wire not_1_out, not_2_out;

  not not_1 (not_1_out, a);
  not not_2 (not_2_out, b);
  or or_1 (intermediate_1, not_1_out, not_2_out);
  or or_2 (intermediate_2, a, b);
  and and_1 (main, intermediate_1, intermediate_2);
endmodule
