// Logisim project McDermottJ_Lab3.circ as structural Verilog: 1 circuit, main circuit main
module main (
  input  in_1,
  input  in_2,
  input  in_3
);

  wire and_1_out, and_2_out, and_3_out, or_1_out, xor_1_out;

  xor xor_1 (xor_1_out, in_1, in_2);
  and and_1 (and_1_out, in_3, in_1);
  and and_2 (and_2_out, in_3, in_2);
  and and_3 (and_3_out, in_2, in_1);
  or or_1 (or_1_out, and_1_out, and_2_out);
  // XOR_Gate xor_2 has open pins: in1=xor_1_out, in4=in_3, out=open
  // OR_Gate or_2 has open pins: in0=or_1_out, in4=and_3_out, out=open
endmodule
