// Logisim project McDermottJ_Lab3part2.circ as structural Verilog: 1 circuit, main circuit main
module main (
  input  in_1,
  input  in_2,
  input  in_3,
  output out_4
);

  wire not_1_out, not_2_out;

  not not_1 (not_1_out, in_1);
  not not_2 (not_2_out, in_2);
  // NOT_Gate not_3 is placed but not wired
  // AND_Gate and_1 has open pins: in0=not_1_out, in2=not_2_out, out=open
  // AND_Gate and_2 has open pins: in0=in_1, out=open
  // OR_Gate or_1 is placed but not wired
endmodule
