// Logisim project McDermottJ_lab3a.circ as structural Verilog: 3 circuits, main circuit main
module main (
  input  X0,
  input  X1,
  input  X2,
  input  X3,
  input  Y0,
  input  Y1,
  input  Y2,
  input  Y3,
  output SUM_0,
  output SUM_1,
  output SUM_2,
  output SUM_3,
  output Last_Carry,
  output OVERFLOW_DETECTED
);

  wire full_adder_1_carry, full_adder_2_carry, full_adder_3_carry;

  Full_Adder full_adder_1 (.X(X0), .Y(Y0), .Z(1'b0), .Sum(SUM_0), .Carry(full_adder_1_carry));
  Full_Adder full_adder_2 (.X(X1), .Y(Y1), .Z(full_adder_1_carry), .Sum(SUM_1), .Carry(full_adder_2_carry));
  Full_Adder full_adder_3 (.X(X2), .Y(Y2), .Z(full_adder_2_carry), .Sum(SUM_2), .Carry(full_adder_3_carry));
  Full_Adder full_adder_4 (.X(X3), .Y(Y3), .Z(full_adder_3_carry), .Sum(SUM_3), .Carry(Last_Carry));
  Overflow_Detector overflow_detector_1 (.X(X3), .Y(Y3), .S(SUM_3), .out_4(OVERFLOW_DETECTED));
endmodule

// FA
module Full_Adder (
  input  X,
  input  Y,
  input  Z,
  output Sum,
  output Carry
);

  wire and_1_out, and_2_out, and_3_out, or_1_out, xor_1_out;

  xor xor_1 (xor_1_out, X, Y);
  and and_1 (and_1_out, Z, X);
  and and_2 (and_2_out, Z, Y);
  and and_3 (and_3_out, Y, X);
  or or_1 (or_1_out, and_1_out, and_2_out);
  xor xor_2 (Sum, xor_1_out, Z);
  or or_2 (Carry, or_1_out, and_3_out);
endmodule

// OF
module Overflow_Detector (
  input  X,
  input  Y,
  input  S,
  output out_4
);

  wire and_1_out, and_2_out, not_1_out, not_2_out, not_3_out;

  not not_1 (not_1_out, S);
  not not_2 (not_2_out, X);
  not not_3 (not_3_out, Y);
  and and_1 (and_1_out, X, Y, not_1_out);
  and and_2 (and_2_out, not_2_out, not_3_out, S);
  or or_1 (out_4, and_2_out, and_1_out);
endmodule
