// Logisim project McDermottJ_lab7.circ as structural Verilog: 1 circuit, main circuit main
module main (
  output bit_0,
  output bit_1,
  output bit_2
);

  wire clock_1_out, j_k_ff_1_q, j_k_ff_2_q;

  Clock clock_1 (.out(clock_1_out));
  J_K_Flip_Flop j_k_ff_1 (
    .J(1'b1), .clk(clock_1_out), .K(1'b1), .Q(j_k_ff_1_q), .Qn(bit_0));  // open: preset, en, reset
  J_K_Flip_Flop j_k_ff_2 (.J(1'b1), .clk(j_k_ff_1_q), .K(1'b1), .Q(j_k_ff_2_q), .Qn(bit_1));  // open: preset, en, reset
  J_K_Flip_Flop j_k_ff_3 (.J(1'b1), .clk(j_k_ff_2_q), .K(1'b1), .Qn(bit_2));  // open: Q, preset, en, reset
endmodule
