// Logisim project McDermottj_lab5.circ as structural Verilog: 2 circuits, main circuit main
module main (
  input  n3,
  input  n2,
  input  n1,
  input  n0,
  output out_5
);

  Prime_Detector prime_detector_1 (.n3(n3), .n2(n2), .n1(n1), .n0(n0), .out_5(out_5));
endmodule

// PD
module Prime_Detector (
  input  n3,
  input  n2,
  input  n1,
  input  n0,
  output out_5
);

  wire and_1_out, and_2_out, and_3_out, xor_1_out;

  and and_1 (and_1_out, n1, ~n2, ~n3);  // AND_Gate
  and and_2 (and_2_out, n0, n2, ~n3);  // AND_Gate
  and and_3 (and_3_out, n0, n3, xor_1_out);
  xor xor_1 (xor_1_out, n1, n2);
  or or_1 (out_5, and_1_out, and_2_out, and_3_out);
endmodule
