// Logisim project McDermottj_lab6.circ as structural Verilog: 2 circuits, main circuit BCD-to-7-Segment Decoder
module BCD_to_7_Segment_Decoder (
  input  d3,
  input  d2,
  input  d1,
  input  d0,
  output out_5,
  output out_6,
  output out_7,
  output out_8,
  output out_9,
  output out_10,
  output g
);

  wire _0_out, _1_out, _2_out, _3_out, _4_out, _5_out, _6_out, _7_out, _8_out, _9_out;

  and _0 (_0_out, ~d3, ~d2, ~d1, ~d0);  // AND_Gate
  and _1 (_1_out, ~d3, ~d2, ~d1, d0);  // AND_Gate
  and _2 (_2_out, ~d3, ~d2, d1, ~d0);  // AND_Gate
  and _3 (_3_out, ~d3, ~d2, d1, d0);  // AND_Gate
  and _4 (_4_out, ~d3, d2, ~d1, ~d0);  // AND_Gate
  and _5 (_5_out, ~d3, d2, ~d1, d0);  // AND_Gate
  and _6 (_6_out, ~d3, d2, d1, ~d0);  // AND_Gate
  and _7 (_7_out, ~d3, d2, d1, d0);  // AND_Gate
  and _8 (_8_out, d3, ~d2, ~d1, ~d0);  // AND_Gate
  and _9 (_9_out, d3, ~d2, ~d1, d0);  // AND_Gate
  or a (out_5, _9_out, _0_out, _2_out, _3_out, _5_out, _6_out, _7_out, _8_out);
  or b (out_6, _0_out, _1_out, _2_out, _3_out, _4_out, _7_out, _8_out, _9_out);
  or c (out_7, _0_out, _1_out, _4_out, _5_out, _6_out, _7_out, _8_out, _9_out);
  or d (out_8, _0_out, _2_out, _3_out, _5_out, _6_out, _8_out, _9_out);
  or e (out_9, _0_out, _2_out, _6_out, _8_out);
  or f (out_10, _0_out, _4_out, _5_out, _6_out, _8_out, _9_out);
  or u_g (g, _2_out, _3_out, _4_out, _5_out, _6_out, _8_out, _9_out);

  // Notes on the sheet:
  //   1
  //   2
  //   0
  //   5
  //   4
  //   3
  //   7
  //   6
  //   8
  //   9
endmodule

module main (
  input  d0,
  input  d1,
  input  d2,
  input  d3
);

  wire BCD_to_7_Segment_Decoder_g, BCD_to_7_Segment_Decoder_out_5, BCD_to_7_Segment_Decoder_out_6,
       BCD_to_7_Segment_Decoder_out_7, BCD_to_7_Segment_Decoder_out_8, BCD_to_7_Segment_Decoder_out_9,
       BCD_to_7_Segment_Decoder_out_10;

  BCD_to_7_Segment_Decoder BCD_to_7_Segment_Decoder (
    .d3(d0), .d2(d1), .d1(d2), .d0(d3), .out_5(BCD_to_7_Segment_Decoder_out_5),
    .out_6(BCD_to_7_Segment_Decoder_out_6), .out_7(BCD_to_7_Segment_Decoder_out_7),
    .out_8(BCD_to_7_Segment_Decoder_out_8), .out_9(BCD_to_7_Segment_Decoder_out_9),
    .out_10(BCD_to_7_Segment_Decoder_out_10), .g(BCD_to_7_Segment_Decoder_g));
  _7_Segment_Display u_7_segment_display_1 (
    .g(BCD_to_7_Segment_Decoder_g), .f(BCD_to_7_Segment_Decoder_out_10), .a(BCD_to_7_Segment_Decoder_out_5),
    .b(BCD_to_7_Segment_Decoder_out_6), .e(BCD_to_7_Segment_Decoder_out_9),
    .d(BCD_to_7_Segment_Decoder_out_8), .c(BCD_to_7_Segment_Decoder_out_7));  // open: dp
endmodule
